# Fritzing sketch WiringDiagram (saved by Fritzing 0.9.2b)
breadboards: 1

parts:
  Part1 = SparkFun ESP8266 Thing  # not connected
  DS1 = DS18B20 1-Wire Temperature Sensor [part_number=DS18B20]
  LED1 = RGB LED - (4 legs) [package="5 mm [THT]"]
  R1 = Resistor [tolerance=±5% resistance=560 package=THT]
  R2 = Resistor [tolerance=±5% resistance=560 package=THT]
  R3 = Resistor [tolerance=±5% resistance=560 package=THT]

nets:
  N1: DS1.VDD, LED1.common_anode
  N2: LED1.red_cathode, R2.Pin_1
  N3: LED1.green_cathode, R3.Pin_1
  N4: LED1.blue_cathode, R1.Pin_1
